# Fritzing sketch Octopus (saved by Fritzing 0.9.5d)
circuit board: 11.332cm x 7.4cm
breadboards: 1

parts:
  Mod1 = Raspberry Pi Pico
  S1 = SWITCH-MOMENTARY-2 [package=tactile-pth-12mm]
  S2 = SWITCH-MOMENTARY-2 [package=tactile-pth-12mm]
  S3 = SWITCH-MOMENTARY-2 [package=tactile-pth-12mm]
  S4 = SWITCH-MOMENTARY-2 [package=tactile-pth-12mm]
  S5 = SWITCH-MOMENTARY-2 [package=tactile-pth-12mm]
  S6 = SWITCH-MOMENTARY-2 [package=tactile-pth-12mm]
  S7 = SWITCH-MOMENTARY-2 [package=tactile-pth-12mm]
  S8 = SWITCH-MOMENTARY-2 [package=tactile-pth-12mm]
  S9 = SWITCH-MOMENTARY-2 [package=tactile-pth-12mm]
  S10 = SWITCH-MOMENTARY-2 [package=tactile-pth-12mm]
  R1 = Resistor [tolerance=±5% resistance=220 package=THT]

nets (from the pcb view):
  N1: Mod1.pin_3, Mod1.pin_6, Mod1.pin_8, Mod1.pin_9, Mod1.pin_10, Mod1.pin_11, Mod1.pin_12, Mod1.pin_13, Mod1.pin_18, Mod1.pin_21, Mod1.pin_22, Mod1.pin_23, Mod1.pin_24, Mod1.pin_25, Mod1.pin_26, Mod1.pin_28, Mod1.pin_33, Mod1.pin_38, Mod1.pin_41, Mod1.pin_42, Mod1.pin_43, S1.2, S2.2, S3.2, S4.2, S5.2, S6.2, S7.2, S8.2, S9.2, S10.2, R1.Pin_0, R1.Pin_1
  N2: Mod1.pin_36, S1.1, S2.1, S3.1, S4.1, S5.1, S6.1, S7.1, S8.1, S9.1, S10.1

notes:
  Octopus 1.1

custom parts:
  Raspberry Pi Pico: Raspberry Pi Pico. Based around the RP2040 microcontroller the Pico is a low cost microcontroller device bringing Raspberry Pi quality, cost, and easy of use to the microcontroller space. Jan 2021, Split part in to two versions: tht (this one) and SMD. This one will drill holes for a .1 in header in pcb to allow plugging in the module as well as providing pads to solder the module to the top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
